// Logisim project 3.2.circ as structural Verilog: 1 circuit, main circuit main
module main (
  input  A,
  input  B,
  input  C,
  input  D,
  output PKNO
);

  wire not_1_out, not_2_out, not_3_out, not_4_out, or_1_out, or_2_out, or_3_out, or_4_out, or_5_out,
       or_6_out, or_7_out;

  not not_1 (not_1_out, A);
  not not_2 (not_2_out, B);
  not not_3 (not_3_out, C);
  not not_4 (not_4_out, D);
  or or_1 (or_1_out, A, B, C, D);
  or or_2 (or_2_out, A, B, C, not_4_out);
  or or_3 (or_3_out, A, B, not_3_out, D);
  or or_4 (or_4_out, A, not_2_out, C, D);
  or or_5 (or_5_out, A, not_2_out, C, not_4_out);
  or or_6 (or_6_out, not_1_out, not_2_out, C, D);
  or or_7 (or_7_out, not_1_out, not_2_out, C, not_4_out);
  and and_1 (PKNO, or_1_out, or_2_out, or_3_out, or_4_out, or_5_out, or_6_out, or_7_out);
endmodule
