// Logisim project V1.circ as structural Verilog: 1 circuit, main circuit main
module main (
  input  x1,
  input  x2,
  input  x3,
  output A
);

  wire and_1_out, not_1_out;

  not not_1 (not_1_out, x2);
  and and_1 (and_1_out, x1, not_1_out);
  or or_1 (A, and_1_out, x3);
endmodule
