// Logisim project V3.1.circ as structural Verilog: 1 circuit, main circuit main
module main (
  input  x1,
  input  x2,
  input  x3,
  output PKNO
);

  wire not_1_out, not_2_out, not_3_out, or_1_out, or_2_out, or_3_out;

  not not_1 (not_1_out, x2);
  not not_2 (not_2_out, x1);
  not not_3 (not_3_out, x2);
  or or_1 (or_1_out, x1, x2, x2);
  or or_2 (or_2_out, x1, not_1_out, x2);
  or or_3 (or_3_out, not_2_out, not_3_out, x2);
  and and_1 (PKNO, or_1_out, or_2_out, or_3_out);

  assign x3 = x2;
endmodule
